# Fritzing sketch project_bt_car (saved by Fritzing 0.9.3b)

parts:
  Part2 = Bluetooth HC-05 Macho
  M2 = DC Motor
  M3 = DC Motor
  M4 = DC Motor
  S1 = H-Bridge with L298N
  M1 = DC Motor
  VCC1 = Battery block 9V  # not connected
  VCC2 = Battery block 9V  # not connected
  Part1 = Arduino Uno (Rev3)

nets:
  N1: Part2.TXD, Part1.D0/RX
  N2: Part2.RXD, Part1.D1/TX
  VCC: Part2.VCC, Part1.5V
  GND: Part2.GND, S1.GND, Part1.GND
  N3: M2.pin_1, S1.M2-01, M1.pin_1
  N4: M2.pin_2, S1.M2-02, M1.pin_2
  N5: M3.pin_1, M4.pin_1, S1.M1-02
  N6: M3.pin_2, M4.pin_2, S1.M1-01
  12V: S1.12V, Part1.VIN
  N7: S1.ENA, Part1.D5_PWM
  N8: S1.IN1, Part1.D6_PWM
  N9: S1.IN2, Part1.D9_PWM
  N10: S1.IN3, Part1.D10_PWM/SS
  N11: S1.IN4, Part1.D11_PWM/MOSI
  N12: S1.ENB, Part1.D12/MISO

notes:
  L298N:
  IN1 → Arduino 8
  IN2 → Arduino 9
  IN3 → Arduino 10
  IN4 → Arduino 11
  ENA & ENB → 5,12
  HC-06:
  VCC → 5V
  GND → GND
  TX → Arduino RX (Pin 0)
  RX → Arduino TX (Pin 1)

custom parts:
  H-Bridge with L298N: h-bridge
